// Digital circuit ALU.dig as structural Verilog
module ALU (
  input  Sum_Substract,
  input  A0,
  input  A1,
  input  A2,
  input  A3,
  input  A4,
  input  A5,
  input  A6,
  input  A7,
  input  B0,
  input  B1,
  input  B2,
  input  B3,
  input  B4,
  input  B5,
  input  B6,
  input  B7,
  output Y0,
  output Y1,
  output Y2,
  output Y3,
  output Y4,
  output Y5,
  output Y6,
  output Y7,
  output Overflow,
  output Zero,
  output Carry_Out,
  output Negative
);

  wire full_adder_1_carry_out, full_adder_2_carry_out, full_adder_3_carry_out, full_adder_4_carry_out,
       full_adder_5_carry_out, full_adder_6_carry_out, full_adder_7_carry_out, or_1_out, or_2_out, xor_1_out,
       xor_2_out, xor_3_out, xor_4_out, xor_5_out, xor_6_out, xor_7_out, xor_8_out;

  xor xor_1 (xor_1_out, Sum_Substract, B0);
  xor xor_2 (xor_2_out, Sum_Substract, B1);
  xor xor_3 (xor_3_out, Sum_Substract, B2);
  xor xor_4 (xor_4_out, Sum_Substract, B3);
  xor xor_5 (xor_5_out, Sum_Substract, B4);
  xor xor_6 (xor_6_out, Sum_Substract, B5);
  xor xor_7 (xor_7_out, Sum_Substract, B6);
  xor xor_8 (xor_8_out, Sum_Substract, B7);
  Full_Adder full_adder_1 (.Carry_In(Sum_Substract), .A(A0), .B(xor_1_out), .Y(Y0), .Carry_out(full_adder_1_carry_out));
  Full_Adder full_adder_2 (
    .Carry_In(full_adder_1_carry_out), .A(A1), .B(xor_2_out), .Y(Y1), .Carry_out(full_adder_2_carry_out));
  Full_Adder full_adder_3 (
    .Carry_In(full_adder_2_carry_out), .A(A2), .B(xor_3_out), .Y(Y2), .Carry_out(full_adder_3_carry_out));
  Full_Adder full_adder_4 (
    .Carry_In(full_adder_3_carry_out), .A(A3), .B(xor_4_out), .Y(Y3), .Carry_out(full_adder_4_carry_out));
  Full_Adder full_adder_5 (
    .Carry_In(full_adder_4_carry_out), .A(A4), .B(xor_5_out), .Y(Y4), .Carry_out(full_adder_5_carry_out));
  Full_Adder full_adder_6 (
    .Carry_In(full_adder_5_carry_out), .A(A5), .B(xor_6_out), .Y(Y5), .Carry_out(full_adder_6_carry_out));
  Full_Adder full_adder_7 (
    .Carry_In(full_adder_6_carry_out), .A(A6), .B(xor_7_out), .Y(Y6), .Carry_out(full_adder_7_carry_out));
  Full_Adder full_adder_8 (
    .Carry_In(full_adder_7_carry_out), .A(A7), .B(xor_8_out), .Y(Negative), .Carry_out(Carry_Out));
  xor xor_9 (Overflow, Carry_Out, full_adder_7_carry_out);
  or or_1 (or_1_out, Y3, Y2, Y1, Y0);
  nor nor_1 (Zero, or_2_out, or_1_out);
  or or_2 (or_2_out, Negative, Y6, Y5, Y4);

  assign Y7 = Negative;
endmodule
