// Digital circuit CPU.dig as structural Verilog
module CPU (
  input  I0,
  input  I1,
  input  I2,
  input  I3,
  input  I4,
  input  I5,
  input  I6,
  input  I7,
  input  WRegB,
  input  WRegA,
  input  ALU_S0,
  input  in_24,
  input  ALU_OUT,
  input  ALU_S1,
  input  ALU_S2,
  input  RegA_OUT,
  input  CLK,
  input  MAR_IN,
  input  RAM_IN,
  input  RAM_OUT,
  input  IR_IN,
  input  PC_OUT,
  input  PC_LOAD,
  input  PC_INC,
  input  RESET,
  output Negative,
  output Carry_out,
  output Zero,
  output Overflow,
  output Y0,
  output Y1,
  output Y2,
  output Y3,
  output Y4,
  output Y5,
  output Y6,
  output Y7
);

  wire flipflop_8bit_1_y0, flipflop_8bit_1_y1, flipflop_8bit_1_y2, flipflop_8bit_1_y3, flipflop_8bit_1_y4,
       flipflop_8bit_1_y5, flipflop_8bit_1_y6, flipflop_8bit_1_y7, flipflop_8bit_3_y0, flipflop_8bit_3_y1,
       flipflop_8bit_3_y2, flipflop_8bit_3_y3, flipflop_8bit_3_y4, flipflop_8bit_3_y5, flipflop_8bit_3_y6,
       flipflop_8bit_3_y7, flipflop_8bit_4_y0, flipflop_8bit_4_y1, flipflop_8bit_4_y2, flipflop_8bit_4_y3,
       flipflop_8bit_4_y4, flipflop_8bit_4_y5, flipflop_8bit_4_y6, flipflop_8bit_4_y7;

  TriState_Switch tristate_switch_1 (
    .Y0(Y0), .Y1(Y1), .Y2(Y2), .Y3(Y3), .Y4(Y4), .Y5(Y5), .Y6(Y6), .Y7(Y7), .I0(I0), .I1(I1), .I2(I2),
    .I3(I3), .I4(I4), .I5(I5), .I6(I6), .I7(I7), .Enable(in_24));
  Flipflop_8bit flipflop_8bit_1 (
    .Y0(flipflop_8bit_1_y0), .Y1(flipflop_8bit_1_y1), .Y2(flipflop_8bit_1_y2), .Y3(flipflop_8bit_1_y3),
    .Y4(flipflop_8bit_1_y4), .Y5(flipflop_8bit_1_y5), .Y6(flipflop_8bit_1_y6), .Y7(flipflop_8bit_1_y7),
    .CLK(CLK), .EN(MAR_IN), .D0(Y0), .D1(Y1), .D2(Y2), .D3(Y3), .D4(Y4), .D5(Y5), .D6(Y6), .D7(Y7));
  RAM_256B ram_256b_1 (
    .D0(Y0), .D1(Y1), .D2(Y2), .D3(Y3), .D4(Y4), .D5(Y5), .D6(Y6), .D7(Y7), .RAM_IN(RAM_IN),
    .RAM_OUT(RAM_OUT), .CLK(CLK), .S0(flipflop_8bit_1_y0), .S1(flipflop_8bit_1_y1), .S2(flipflop_8bit_1_y2),
    .S3(flipflop_8bit_1_y3), .S4(flipflop_8bit_1_y4), .S5(flipflop_8bit_1_y5), .S6(flipflop_8bit_1_y6),
    .S7(flipflop_8bit_1_y7), .Y0(Y0), .Y1(Y1), .Y2(Y2), .Y3(Y3), .Y4(Y4), .Y5(Y5), .Y6(Y6), .Y7(Y7));
  Flipflop_8bit flipflop_8bit_2 (
    .CLK(CLK), .EN(IR_IN), .D0(Y0), .D1(Y1), .D2(Y2), .D3(Y3), .D4(Y4), .D5(1'b0), .D6(1'b0), .D7(1'b0));  // open: Y0, Y1, Y2, Y3, Y4, Y5, Y6, Y7
  PC_Counter pc_counter_1 (
    .PC_OUT(PC_OUT), .PC_inc(PC_INC), .PC_load(PC_LOAD), .Reset(RESET), .CLK(CLK), .Din0(Y0), .Din1(Y1),
    .Din2(Y2), .Din3(Y3), .Din4(Y4), .Din5(Y5), .Din6(Y6), .Din7(Y7), .Y0(Y0), .Y1(Y1), .Y2(Y2), .Y3(Y3),
    .Y4(Y4), .Y5(Y5), .Y6(Y6), .Y7(Y7));  // open: Zero
  Flipflop_8bit flipflop_8bit_3 (
    .Y0(flipflop_8bit_3_y0), .Y1(flipflop_8bit_3_y1), .Y2(flipflop_8bit_3_y2), .Y3(flipflop_8bit_3_y3),
    .Y4(flipflop_8bit_3_y4), .Y5(flipflop_8bit_3_y5), .Y6(flipflop_8bit_3_y6), .Y7(flipflop_8bit_3_y7),
    .CLK(WRegA), .EN(1'b1), .D0(Y0), .D1(Y1), .D2(Y2), .D3(Y3), .D4(Y4), .D5(Y5), .D6(Y6), .D7(Y7));
  Flipflop_8bit flipflop_8bit_4 (
    .Y0(flipflop_8bit_4_y0), .Y1(flipflop_8bit_4_y1), .Y2(flipflop_8bit_4_y2), .Y3(flipflop_8bit_4_y3),
    .Y4(flipflop_8bit_4_y4), .Y5(flipflop_8bit_4_y5), .Y6(flipflop_8bit_4_y6), .Y7(flipflop_8bit_4_y7),
    .CLK(WRegB), .EN(1'b1), .D0(Y0), .D1(Y1), .D2(Y2), .D3(Y3), .D4(Y4), .D5(Y5), .D6(Y6), .D7(Y7));
  TriState_Switch tristate_switch_2 (
    .Y0(Y0), .Y1(Y1), .Y2(Y2), .Y3(Y3), .Y4(Y4), .Y5(Y5), .Y6(Y6), .Y7(Y7), .I0(flipflop_8bit_3_y0),
    .I1(flipflop_8bit_3_y1), .I2(flipflop_8bit_3_y2), .I3(flipflop_8bit_3_y3), .I4(flipflop_8bit_3_y4),
    .I5(flipflop_8bit_3_y5), .I6(flipflop_8bit_3_y6), .I7(flipflop_8bit_3_y7), .Enable(RegA_OUT));
  FULL_ALU full_alu_1 ();
  Seven_Seg_Hex seven_seg_hex_1 (.d({Y7, Y6, Y5, Y4}), .dp(1'b0));
  Seven_Seg_Hex seven_seg_hex_2 (.d({Y3, Y2, Y1, Y0}), .dp(1'b0));

  // Notes on the sheet:
  //   MAR
  //   00001 - LDA
  //   00010 - ADD
  //   00011 - Subs
  //   00100 -  STA
  //   00101 - LDI
  //   00110 - JMP
  //   00111 - JMP if Carry (JC)
  //   01000 - JMP IF Zero (JZ)
  //   01001 - JMP IF Negative
  //   01010 - JMP IF OVERFLOW
  //   01011 - OR
  //   01100 - AND
  //   01101 - XOR
  //   01110 - ASR
  //   01111 - LSL
  //   10000 - LSR
  //   10001 - CMP
  //   10010 - INC 
  //   10011 - DEC
  //   11111 - HLT (Stop the computer)
  //   000 ----> Add
  //   001 ----> Substract
  //   010  -----> AND	
  //   011 -------> OR
  //   100   -------> XOR
  //   101 ---------> ASR
  //   110 ----------> LSL
  //   111 ----------> LSR
endmodule
