// Digital circuit RAM.dig as structural Verilog
module RAM (
  input  S0,
  input  S1,
  input  S2,
  input  S3
);

  wire not_1_out, not_2_out;

  not not_1 (not_1_out, S0);
  not not_2 (not_2_out, S1);
endmodule
